// Logisim project Team115.circ as structural Verilog: 4 circuits, main circuit main
module main (
  input  in_1,
  input  in_2,
  input  in_3,
  input  in_4,
  input  in_5,
  input  in_6,
  input  in_7,
  input  in_8,
  input  in_9,
  input  in_10,
  input  in_11,
  input  in_12
);

  wire ALU_eout, CLK, D1T5, D2T5, D3T4, D7_IT3, DR, E_q, lcu_1_d1t4, lcu_1_d2t4, M0, M1, M2, or_1_out,
       or_2_out, RB0, RB5, RB6, RB9, RB11, ReadMemory, T0, T1, T2, t_ff_1_qn;
  wire [3:0] undriven;
  wire [7:0] bit_extender_1_out, INPR_q;
  wire [11:0] AR_q, bit_extender_2_out, bit_extender_3_out, bitselector_1_out, PC_q;
  wire [15:0] AC_q, ALU_ac_2, bit_extender_4_out, bit_extender_5_out, bit_extender_6_out, DR_q,
       multiplexer_1_out, ram_1_data, Tm;

  Clock clock_1 (.out(CLK));
  Bit_Extender #(.in_width(16), .out_width(8)) bit_extender_1 (.in(multiplexer_1_out), .out(bit_extender_1_out));
  ALU ALU (
    .AC(AC_q), .DR(DR_q), .INPR(INPR_q), .Ein(E_q), .Circular_left_with_E(RB6), .Circular_right_with_E(in_5),
    .Complement_AC(RB9), .Transfer_INP(in_3), .Transfer_DR(D2T5), .ADD(D1T5), .AND(in_4), .Eout(ALU_eout),
    .AC_2(ALU_ac_2));
  T_Flip_Flop t_ff_1 (.clk(CLK), .T(RB0), .Qn(t_ff_1_qn));  // open: Q, preset, reset, en
  Bit_Extender #(.in_width(16), .out_width(12)) bit_extender_2 (.in(multiplexer_1_out), .out(bit_extender_2_out));
  Bit_Extender #(.in_width(16), .out_width(12)) bit_extender_3 (.in(multiplexer_1_out), .out(bit_extender_3_out));
  D_Flip_Flop E (.clk(CLK), .D(ALU_eout), .Q(E_q));  // open: Qn, preset, en, reset
  or or_1 (or_1_out, D2T5, D1T5, RB9);
  or or_2 (or_2_out, T0, D7_IT3, T2);
  Counter #(.width(12), .max('hfff)) AR (
    .load(or_2_out), .D(bit_extender_2_out), .count(in_6), .Q(AR_q), .clk(CLK));  // open: carry, clr
  Counter #(.width(12), .max('hfff)) PC (
    .load(in_1), .D(bit_extender_3_out), .count(T1), .Q(PC_q), .clk(CLK));  // open: carry, clr
  Counter #(.width(16), .max('hffff)) u_DR (
    .load(DR), .D(multiplexer_1_out), .count(in_7), .Q(DR_q), .clk(CLK));  // open: carry, clr
  Counter #(.width(16), .max('hffff)) AC (
    .load(or_1_out), .D(ALU_ac_2), .count(RB5), .Q(AC_q), .clk(CLK), .clr(RB11));  // open: carry
  Register INPR (.en(in_8), .Q(INPR_q), .clk(CLK));  // open: D, clr
  Counter #(.width(16), .max('hffff)) IR (
    .load(T1), .D(multiplexer_1_out), .count(in_9), .Q(Tm), .clk(CLK));  // open: carry, clr
  Counter OUTR (.load(in_2), .D(bit_extender_1_out), .count(in_11), .clk(CLK));  // open: Q, carry, clr
  LCU lcu_1 (
    .IR_Input(Tm), .T0(T0), .BitSelector(3'b100), .Clock(CLK), .LD_Signal(in_12), .Input_Data(undriven),
    .RB9(RB9), .RB5(RB5), .RB11(RB11), .RB0(RB0), .RB6(RB6), .D2T4(lcu_1_d2t4), .D2T5(D2T5),
    .D1T4(lcu_1_d1t4), .D1T5(D1T5), .D7I_T3(D7_IT3), .D3T4(D3T4), .T1(T1), .INR(t_ff_1_qn), .M2(M2), .M1(M1),
    .M0(M0), .T2(T2), .Read_Memory(ReadMemory));
  or or_3 (DR, lcu_1_d2t4, lcu_1_d1t4);
  RAM #(.addrWidth(12), .dataWidth(16), .bus("separate")) ram_1 (
    .addr(AR_q), .din(multiplexer_1_out), .data(ram_1_data), .str(D3T4), .clk(CLK), .ld(ReadMemory));  // open: sel, clr
  BitSelector #(.width(16), .group(12)) bitselector_1 (.in(Tm), .out(bitselector_1_out), .sel(in_10));
  assign bit_extender_4_out = {{4{1'b0}}, bitselector_1_out};  // Bit_Extender bit_extender_4
  assign bit_extender_5_out = {{4{1'b0}}, AR_q};  // Bit_Extender bit_extender_5
  assign bit_extender_6_out = {{4{1'b0}}, PC_q};  // Bit_Extender bit_extender_6
  Multiplexer #(.select(3), .width(16), .enable("false")) multiplexer_1 (
    .in1(bit_extender_5_out), .in2(bit_extender_6_out), .in3(DR_q), .in4(AC_q), .in5(bit_extender_4_out),
    .in7(ram_1_data), .out(multiplexer_1_out), .sel({M0, M1, M2}));  // open: in0, in6
endmodule

module ALU (
  input  AND,
  input  ADD,
  input  Transfer_DR,
  input  Transfer_INP,
  input  Complement_AC,
  input  Circular_right_with_E,
  input  Circular_left_with_E,
  input  [15:0] AC,
  input  [15:0] DR,
  input  [7:0] INPR,
  input  Ein,
  output [15:0] AC_2,
  output Eout
);

  wire adder_1_cout, not_2_out;
  wire [1:0] bit_extender_1_out, or_1_out;
  wire [2:0] priority_encoder_1_out;
  wire [15:0] adder_1_out, and_1_out, bit_extender_2_out, not_1_out;

  Priority_Encoder priority_encoder_1 (
    .in0(AND), .in1(ADD), .in2(Transfer_DR), .in3(Transfer_INP), .in4(Complement_AC),
    .in5(Circular_right_with_E), .in6(Circular_left_with_E), .out(priority_encoder_1_out));  // open: in7, en_in, gs, en_out
  assign and_1_out = AC & DR;  // AND_Gate and_1, 16 bits wide
  assign bit_extender_1_out = {{1{ADD}}, ADD};  // Bit_Extender bit_extender_1
  Adder #(.width(16)) adder_1 (.a(AC), .b(DR), .out(adder_1_out), .cout(adder_1_cout));  // open: cin
  assign bit_extender_2_out = {{8{1'b0}}, INPR};  // Bit_Extender bit_extender_2
  Multiplexer #(.select(3), .width(16), .enable("false")) multiplexer_1 (
    .in0(and_1_out), .in1(adder_1_out), .in2(DR), .in3(bit_extender_2_out), .in4(not_1_out),
    .in5({Ein, AC[15:1]}), .in6({AC[14:0], Ein}), .out(AC_2), .sel(priority_encoder_1_out));  // open: in7
  assign not_1_out = ~AC;  // NOT_Gate not_1, 16 bits wide
  assign or_1_out = bit_extender_1_out | {Circular_left_with_E, Circular_right_with_E};  // OR_Gate or_1, 2 bits wide
  Multiplexer #(.select(2), .disabled(0), .enable("false")) multiplexer_2 (
    .in0(not_2_out), .in1(AC[0]), .in2(AC[15]), .in3(adder_1_cout), .out(Eout), .sel(or_1_out));
  not not_2 (not_2_out, 1'b1);
endmodule

// sc counter
module SC_Counter (
  input  LD_SIGNAL,
  input  [3:0] input_data,
  input  INR_SIGNAL,
  input  Clock,
  input  CLR_SIGNALL,
  output [3:0] out_6
);

  wire d_ff_1_q;
  wire [3:0] counter_1_q;

  Counter #(.width(4), .max('hf)) counter_1 (
    .load(LD_SIGNAL), .D(input_data), .count(INR_SIGNAL), .Q(counter_1_q), .clk(Clock), .clr(d_ff_1_q));  // open: carry
  D_Flip_Flop d_ff_1 (.clk(Clock), .D(CLR_SIGNALL), .Q(d_ff_1_q));  // open: Qn, preset, en, reset
  Bit_Extender #(.in_width(4), .out_width(4)) bit_extender_1 (.in(counter_1_q), .out(out_6));
endmodule

module LCU (
  input  [15:0] IR_Input,
  input  [2:0] BitSelector,
  input  Clock,
  input  LD_Signal,
  input  INR,
  input  [3:0] Input_Data,
  output T0,
  output RB9,
  output RB5,
  output RB11,
  output RB0,
  output RB6,
  output D2T4,
  output D2T5,
  output D1T4,
  output D1T5,
  output D7I_T3,
  output D3T4,
  output T1,
  output M2,
  output M1,
  output M0,
  output T2,
  output Read_Memory
);

  wire D1, D2, D3, D4, D5, D6, D7, I_star, not_1_out, not_2_out, or_1_out, R, T3, T4, T5, X4;
  wire [2:0] bitselector_1_out;
  wire [3:0] sc_counter_1_out_6;

  D_Flip_Flop d_ff_1 (.clk(Clock), .D(IR_Input[15]), .Qn(I_star));  // open: Q, preset, en, reset
  Decoder #(.select(4), .enable("false")) decoder_1 (
    .out0(T0), .out1(T1), .out2(T2), .out3(T3), .out4(T4), .out5(T5), .sel(sc_counter_1_out_6));  // open: out6, out7, out8, out9, out10, out11, out12, out13, out14, out15
  SC_Counter sc_counter_1 (
    .LD_SIGNAL(LD_Signal), .input_data(Input_Data), .INR_SIGNAL(INR), .Clock(Clock), .CLR_SIGNALL(or_1_out),
    .out_6(sc_counter_1_out_6));
  or or_1 (or_1_out, D3T4, X4, D1T5, D2T5);
  BitSelector #(.width(16), .group(3)) bitselector_1 (.in(IR_Input), .out(bitselector_1_out), .sel(BitSelector));
  Decoder #(.select(3), .enable("false")) decoder_2 (
    .out1(D1), .out2(D2), .out3(D3), .out4(D4), .out5(D5), .out6(D6), .out7(D7), .sel(bitselector_1_out));  // open: out0
  and D7T3I_star (R, D7, T3, I_star);
  not not_1 (not_1_out, D7);
  not not_2 (not_2_out, I_star);
  and D7_IT3 (D7I_T3, not_1_out, not_2_out, T3);
  and ADD2 (D1T5, D1, T5);
  and STA (D3T4, D3, T4);
  and CMA (RB9, IR_Input[9], R);
  and INC (RB5, IR_Input[5], R);
  and CLA (RB11, IR_Input[11], R);
  and HLT (RB0, R, IR_Input[0]);
  and CIL (RB6, R, IR_Input[6]);
  and LDA (D2T4, D2, T4);
  and LDA2 (D2T5, D2, T5);
  and ADD (D1T4, D1, T4);
  or or_2 (X4, RB9, RB5, RB11, RB0, RB6);
  or or_3 (M2, D2T5, D2T4, D1T4, T1, T2);
  or or_4 (M1, D2T5, D2T4, D1T4, T0, T1);
  or or_5 (M0, D2T4, D1T4, D3T4, T1, T2);
  or or_6 (Read_Memory, D2T4, D1T4, D7I_T3, T1);

  // Other names for the same wires on the sheet: B0 = IR_Input[0]; B1 = IR_Input[1]; B2 = IR_Input[2];
  //   B3 = IR_Input[3]; B5 = IR_Input[5]; B6 = IR_Input[6]; B9 = IR_Input[9]; B11 = IR_Input[11]; B15 = IR_Input[15];
  //   X1 = D2T5; X2 = D1T5; X3 = D3T4
endmodule
